# Fritzing sketch awning_control_perfboard_v1.0 (saved by Fritzing 0.9.4)
perfboards: 1

parts:
  U1 = NodeMCU V1.0
  U2 = FS1000A - 433Mhz RF Transmitter [package=THT]
  Antenna1 = HC-12 Antenna

nets:
  N1: U1.D0, U2.DATA
  3V3: U1.3V3, U2.VCC
  GND: U1.GND, U2.GND
  N2: U2.Antenna, Antenna1.ANT

custom parts:
  NodeMCU V1.0: ESP8266 based NodeMCU
  FS1000A - 433Mhz RF Transmitter: This is 433Mhz RF transmitter with receiver kit for Arduino ARM MCU wireless Application environment: Remote control switch, receiver module, motorcycles, automobile anti-theft products, home security products, electric doors, shutter doors, windows, remote control socket, remote control LED, remote audio remote control electric doors, garage door remote control, remote control retractable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
  HC-12 Antenna: Antenna for HC-12 433Mhz Module
